# Fritzing sketch circuit (saved by Fritzing 0.9.2b)
breadboards: 1

parts:
  S1 = Pushbutton [package="[THT]"]
  LED1 = LED - 5mm [color="Red (633nm)" package="5 mm [THT]"]
  R1 = Resistor [tolerance=±5% resistance=100 package="0402 [SMD]"]
  Bauteil1 = Arduino Mega 2560 (Rev3)

nets:
  N1: S1.Pin_1, S1.Pin_2, Bauteil1.GND
  N2: S1.Pin_3, S1.Pin_4, Bauteil1.D3_PWM
  N3: LED1.cathode, R1.Pin_0
  N4: LED1.anode, Bauteil1.D2_PWM
